# Fritzing sketch RZ67 Seeed XIAO ESP32C3 (saved by Fritzing 0.9.10b)
breadboards: 1

parts:
  Q1 = Basic FET N-Channel [package="DPak [SMD]"]
  J1 = female pin header, 3 pins [form="♀ (female)"]
  J2 = male pin header, 7 pins [form="♂ (male)"]
  J3 = male pin header, 7 pins [form="♂ (male)"]
  U1 = LIPO-110mAh [package=lipo-110]
  A1 = XIAO ESP32C3-smd

nets:
  N1: Q1.Gate, J2.pin7, A1.Pin_15
  N2: Q1.drain, J1.pin1
  N3: Q1.source, J1.pin2, J1.pin3, J3.pin2, A1.Pin_2, A1.Pin_21
  N4: J2.pin1, A1.Pin_9
  N5: J2.pin2, A1.Pin_10
  N6: J2.pin3, A1.Pin_11
  N7: J2.pin4, A1.Pin_12
  N8: J2.pin5, A1.Pin_13
  N9: J2.pin6, A1.Pin_14
  N10: J3.pin1, A1.Pin_22
  N11: J3.pin3, A1.Pin_20
  N12: J3.pin4, A1.Pin_19
  N13: J3.pin5, A1.Pin_18
  N14: J3.pin6, A1.Pin_17
  N15: J3.pin7, A1.Pin_16
  N16: U1.+, A1.Pin_8
  N17: U1.-, A1.Pin_7

notes:
  Header is to illustrate cable to Mamiya RZ67.
  Mamiya's pinout is, from left to right:
  - 6V PWR
  - GRD
  - S1
  - S2
  To trigger the shutter release from the ESP32, we need to connect GND, S1 and S2 via the MOSFET. PWR can be ignored.

custom parts:
  XIAO ESP32C3-smd: Seeed Studio XIAO ESP32C3 adopts new RISC-V architecture, supporting both Wi-Fi and BLE wireless connectivities.
